# Fritzing sketch breadboard (saved by Fritzing 0.9.3b)
breadboards: 2

parts:
  Part1 = Arduino Uno (Rev3)
  hc-sr1 = hc-sr04
  hc-sr2 = hc-sr04
  hc-sr3 = hc-sr04
  hc-sr4 = hc-sr04
  S1 = Pushbutton [package="[THT]"]
  R1 = Resistor [tolerance=±5% resistance=10k package="0805 [SMD]"]
  U1 = Vibration Motor- ROB-08449 [package=vibe-motor-10mm]
  U2 = Vibration Motor- ROB-08449 [package=vibe-motor-10mm]
  U3 = Vibration Motor- ROB-08449 [package=vibe-motor-10mm]
  BAT1 = BC9VPC [package=bc9vpc]

nets:
  N1: Part1.A0, S1.Pin_3, S1.Pin_4, R1.Pin_1
  N2: Part1.D8, hc-sr4.Echo
  N3: Part1.D9_PWM, U3.-
  N4: Part1.D10_PWM/SS, U1.-
  N5: Part1.D11_PWM/MOSI, U2.-
  N6: Part1.D1/TX, hc-sr1.Trig
  N7: Part1.D2, hc-sr2.Trig
  N8: Part1.D3_PWM, hc-sr3.Trig
  N9: Part1.D4, hc-sr4.Trig
  N10: Part1.D5_PWM, hc-sr1.Echo
  N11: Part1.D6_PWM, hc-sr2.Echo
  N12: Part1.D7, hc-sr3.Echo
  VCC: Part1.5V, hc-sr1.VCC, hc-sr2.VCC, hc-sr3.VCC, hc-sr4.VCC, S1.Pin_1, S1.Pin_2
  GND: Part1.GND, hc-sr1.GND, hc-sr2.GND, hc-sr3.GND, hc-sr4.GND, R1.Pin_0, U1.+, U2.+, U3.+, BAT1.V+
  N13: Part1.VIN, BAT1.V-
